// Logisim project B2_G1.circ as structural Verilog: 3 circuits, main circuit DataMemory
module Control (
  input  [3:0] Opcode,
  output RegDst,
  output Jump,
  output Branch,
  output MemRead,
  output MemtoReg,
  output [3:0] ALUop,
  output MemWrite,
  output ALUSrc,
  output RegWrite,
  output Shift
);

  wire [15:13] rom_1_data;

  ROM #(.addrWidth(4), .dataWidth(16)) rom_1 (
    .addr(Opcode),
    .data({rom_1_data, Shift, RegWrite, ALUSrc, MemWrite, ALUop, MemtoReg, MemRead, Branch, Jump, RegDst}));  // open: sel

  // Notes on the sheet:
  //   contents of rom_1 (hex, n*v repeats v):
  //   881 801 d00 861 c00 8c1 1821 1921 600 4 cc0 4 2 c80 c18 901
endmodule

module DataMemory (
  input  [7:0] Address,
  input  [7:0] WriteData,
  input  CLK,
  input  MemWrite,
  input  MemRead,
  output [7:0] ReadData
);

  RAM #(.bus("separate")) ram_1 (
    .addr(Address), .din(WriteData), .data(ReadData), .str(MemWrite), .clk(CLK), .ld(MemRead), .clr(1'b0));  // open: sel
endmodule

module Main (
);

  wire and_1_out, clock_1_out, control_1_alusrc, control_1_branch, control_1_jump, control_1_memread,
       control_1_memtoreg, control_1_memwrite, control_1_shift, mips_alu_1_p4;
  wire [3:0] control_1_aluop;
  wire [7:0] adder_1_out, adder_2_out, Data_Memory_readdata, multiplexer_3_out, multiplexer_4_out, PC_q,
       undriven;
  wire [31:0] bit_extender_1_out, mips_alu_1_p5, multiplexer_1_out, multiplexer_2_out;

  Clock clock_1 (.out(clock_1_out));
  Register PC (.D(multiplexer_4_out), .en(1'b1), .Q(PC_q), .clk(clock_1_out));  // open: clr
  Adder adder_1 (.a(PC_q), .b(8'h1), .out(adder_1_out));  // open: cin, cout
  Control control_1 (
    .Jump(control_1_jump), .Branch(control_1_branch), .MemRead(control_1_memread),
    .MemtoReg(control_1_memtoreg), .ALUop(control_1_aluop), .MemWrite(control_1_memwrite),
    .ALUSrc(control_1_alusrc), .Shift(control_1_shift));  // open: Opcode, RegDst, RegWrite
  assign bit_extender_1_out = {{24{undriven[7]}}, undriven};  // Bit_Extender bit_extender_1
  Multiplexer #(.width(32), .enable("false")) multiplexer_1 (
    .out(multiplexer_1_out), .sel(control_1_shift));  // open: in0, in1
  Multiplexer #(.width(32), .enable("false")) multiplexer_2 (
    .in1(bit_extender_1_out), .out(multiplexer_2_out), .sel(control_1_alusrc));  // open: in0
  Adder adder_2 (.a(adder_1_out), .b(undriven), .out(adder_2_out));  // open: cin, cout
  // MIPS_ALU mips_alu_1: pin names not known; wires that end beside it: multiplexer_1_out, multiplexer_2_out, control_1_aluop, mips_alu_1_p4, mips_alu_1_p5
  and and_1 (and_1_out, mips_alu_1_p4, control_1_branch);
  Multiplexer #(.width(8), .enable("false")) multiplexer_3 (
    .in0(adder_1_out), .in1(adder_2_out), .out(multiplexer_3_out), .sel(and_1_out));
  DataMemory Data_Memory (
    .Address(mips_alu_1_p5[7:0]), .MemWrite(control_1_memwrite), .MemRead(control_1_memread),
    .ReadData(Data_Memory_readdata));  // open: WriteData, CLK
  Multiplexer #(.width(8), .enable("false")) multiplexer_4 (
    .in0(multiplexer_3_out), .out(multiplexer_4_out), .sel(control_1_jump));  // open: in1
  Multiplexer #(.width(8), .enable("false")) multiplexer_5 (
    .in0(mips_alu_1_p5[7:0]), .in1(Data_Memory_readdata), .sel(control_1_memtoreg));  // open: out
endmodule
